# Fritzing sketch attiny85AutoOff1Pin (saved by Fritzing 0.9.3b)
circuit board: 4.44176cm x 3.60024cm
breadboards: 1

parts:
  VCC1 = 4 x AAA Battery Mount
  R3 = Resistor [tolerance=±5% resistance=100k package=THT]
  R2 = Resistor [tolerance=±5% resistance=100k package=THT]
  R4 = Resistor [tolerance=±5% resistance=50k package=THT]
  S1 = Pushbutton [package="[THT]"]
  U2 = attiny85 [package=dip]
  Q1 = NPN-Transistor [package="TO92 [THT]"]
  Q2 = PNP-Transistor [package="TO92 [THT]"]
  R1 = Resistor [tolerance=±5% resistance=100k package=THT]

nets:
  GND: VCC1.-, R4.Pin_0, U2.Pin_4, Q1.E
  N1: VCC1.+, R2.Pin_0, S1.Pin_1, S1.Pin_2, Q2.E
  N2: R3.Pin_0, Q2.B
  N3: R3.Pin_1, R2.Pin_1, Q1.C
  N4: R4.Pin_1, S1.Pin_3, S1.Pin_4, U2.Pin_2, R1.Pin_1
  N5: U2.Pin_8, Q2.C
  N6: Q1.B, R1.Pin_0

notes:
  V+
  GND
  SCL
  SDA
  KEEP ON / READ BUTTON
